# Fritzing sketch Resistor Puzzle (saved by Fritzing 0.9.2b)
circuit board: 8.46667cm x 5.64444cm
breadboards: 2

parts:
  R1 = Resistor [tolerance=±5% resistance=220 package=THT]
  R2 = Resistor [tolerance=±5% resistance=220 package=THT]
  R3 = Resistor [tolerance=±5% resistance=220 package=THT]
  R4 = Resistor [tolerance=±5% resistance=220 package=THT]
  U2 = SWITCH-SPST-2 [package=switch-spst-vertical]
  U1 = SWITCH-SPST-2 [package=switch-spst-vertical]
  U4 = SWITCH-SPST-2 [package=switch-spst-vertical]
  U5 = SWITCH-SPST-2 [package=switch-spst-vertical]
  U6 = SWITCH-SPST-2 [package=switch-spst-vertical]
  U7 = SWITCH-SPST-2 [package=switch-spst-vertical]
  U8 = SWITCH-SPST-2 [package=switch-spst-vertical]
  U9 = SWITCH-SPST-2 [package=switch-spst-vertical]
  R5 = Resistor [tolerance=±5% resistance=220 package=THT]
  R6 = Resistor [tolerance=±5% resistance=220 package=THT]
  R7 = Resistor [tolerance=±5% resistance=220 package=THT]
  R8 = Resistor [tolerance=±5% resistance=220 package=THT]
  R9 = Resistor [tolerance=±5% resistance=220 package=THT]
  JACK1 = 2.1mm Barrel Jack with Terminal Block
  U3 = SWITCH-SPST-2 [package=switch-spst-vertical]

nets:
  N1: R1.Pin_0, R2.Pin_0, R3.Pin_0, JACK1.POS
  N2: R1.Pin_1, U1.O
  N3: R2.Pin_1, U2.O
  N4: R3.Pin_1, U3.O
  N5: R4.Pin_0, U2.P, U1.P, R5.Pin_0, R6.Pin_0, U3.P
  N6: R4.Pin_1, U4.O
  N7: U4.P, U5.P, U6.P, R7.Pin_0, R8.Pin_0, R9.Pin_0
  N8: U5.O, R5.Pin_1
  N9: U6.O, R6.Pin_1
  N10: U7.O, R7.Pin_1
  N11: U7.P, U8.P, U9.P, JACK1.NEG
  N12: U8.O, R8.Pin_1
  N13: U9.O, R9.Pin_1
