# Fritzing sketch Simulator 0.1 (saved by Fritzing 0.9.2b)
breadboards: 2

parts:
  BeagleBone2 = BeagleBone Black
  R1 = Resistor [tolerance=±0.1% resistance=1.5k package=THT]
  Part1 = Logic Level Converter
  R5 = Resistor [tolerance=±0.1% resistance=1.5k package=THT]
  R2 = Resistor [tolerance=±0.1% resistance=100 package=THT]
  R6 = Resistor [tolerance=±0.1% resistance=100 package=THT]
  R3 = Resistor [tolerance=±0.1% resistance=750 package=THT]
  R4 = Resistor [tolerance=±0.1% resistance=150 package=THT]
  R7 = Resistor [tolerance=±0.1% resistance=750 package=THT]
  R8 = Resistor [tolerance=±0.1% resistance=150 package=THT]
  7SEG1 = 7-Segment LED I2C Backpack (white)
  Power_+5V = Power plug
  7SEG2 = 7-Segment LED I2C Backpack (white)
  7SEG3 = 7-Segment LED I2C Backpack (white)
  7SEG4 = 7-Segment LED I2C Backpack (white)
  7SEG5 = 7-Segment LED I2C Backpack (white)
  7SEG6 = 7-Segment LED I2C Backpack (white)
  7SEG7 = 7-Segment LED I2C Backpack (white)
  7SEG8 = 7-Segment LED I2C Backpack (white)
  7SEG9 = 7-Segment LED I2C Backpack (white)

nets:
  N1: BeagleBone2.DGND, BeagleBone2.GNDA_ADC, Part1.HV, R4.Pin_1, R8.Pin_1
  N2: BeagleBone2.VDD_3V3, Part1.GND
  N3: BeagleBone2.I2C2_SCL, Part1.TX2_HV
  N4: BeagleBone2.I2C2_SDA, Part1.RX2_HV
  N5: BeagleBone2.AIN0, R2.Pin_1, R3.Pin_0
  N6: BeagleBone2.AIN1, R6.Pin_1, R7.Pin_0
  N7: R1.Pin_1, R2.Pin_0
  N8: Part1.TX2_LV, 7SEG1.SCL, 7SEG2.SCL, 7SEG3.SCL, 7SEG4.SCL, 7SEG5.SCL, 7SEG6.SCL, 7SEG7.SCL, 7SEG8.SCL, 7SEG9.SCL
  N9: Part1.RX2_LV, 7SEG1.SDA, 7SEG2.SDA, 7SEG3.SDA, 7SEG4.SDA, 7SEG5.SDA, 7SEG6.SDA, 7SEG7.SDA, 7SEG8.SDA, 7SEG9.SDA
  N10: R5.Pin_1, R6.Pin_0
  N11: R3.Pin_1, R4.Pin_0
  N12: R7.Pin_1, R8.Pin_0
  N13: 7SEG1.V+, Power_+5V.VCC, 7SEG2.V+, 7SEG3.V+, 7SEG4.V+, 7SEG5.V+, 7SEG6.V+, 7SEG7.V+, 7SEG8.V+, 7SEG9.V+
  GND: 7SEG1.GND, Power_+5V.GND, 7SEG2.GND, 7SEG3.GND, 7SEG4.GND, 7SEG5.GND, 7SEG6.GND, 7SEG7.GND, 7SEG8.GND, 7SEG9.GND

custom parts:
  BeagleBone Black: BeagleBone Black rev. A5B
  7-Segment LED I2C Backpack (white): 4-digit, 7-segment LED Display with I2C Control
