# Fritzing sketch Simulator 0.3 (saved by Fritzing 0.9.2b)
breadboards: 1

parts:
  MASS1 = OpenSegment Serial Display - 20mm (Blue) [part_number=COM-11647]
  IC1 = DIP - 14 pins [chip_label=IC package="DIP (Dual Inline) [THT]"]
  Part1 = Bi-Directional Logic Level Converter [part_number=BOB-12009]
  BeagleBone1 = BeagleBone Black
  MASS2 = OpenSegment Serial Display - 20mm (Blue) [part_number=COM-11647]
  PRESSURE1 = OpenSegment Serial Display - 20mm (Blue) [part_number=COM-11647]
  MASS3 = OpenSegment Serial Display - 20mm (Blue) [part_number=COM-11647]
  PRESSURE2 = OpenSegment Serial Display - 20mm (Blue) [part_number=COM-11647]
  MASS4 = OpenSegment Serial Display - 20mm (Blue) [part_number=COM-11647]
  MASS5 = OpenSegment Serial Display - 20mm (Blue) [part_number=COM-11647]
  PRESSURE3 = OpenSegment Serial Display - 20mm (Blue) [part_number=COM-11647]
  MASS6 = OpenSegment Serial Display - 20mm (Blue) [part_number=COM-11647]
  INA1 = INA219 DC Current Sensor Breakout
  R1 = Resistor [tolerance=±5% resistance=220 package=THT]
  R2 = Resistor [tolerance=±5% resistance=220 package=THT]
  R3 = Resistor [tolerance=±5% resistance=220 package=THT]
  R4 = Resistor [tolerance=±5% resistance=220 package=THT]
  R5 = Resistor [tolerance=±5% resistance=220 package=THT]
  R6 = Resistor [tolerance=±5% resistance=220 package=THT]
  R7 = Resistor [tolerance=±5% resistance=220 package=THT]
  R8 = Resistor [tolerance=±5% resistance=220 package=THT]
  R9 = Resistor [tolerance=±5% resistance=220 package=THT]
  U1 = SWITCH-SPST-2 [package=switch-spst-vertical]
  U2 = SWITCH-SPST-2 [package=switch-spst-vertical]
  U3 = SWITCH-SPST-2 [package=switch-spst-vertical]
  U4 = SWITCH-SPST-2 [package=switch-spst-vertical]
  U5 = SWITCH-SPST-2 [package=switch-spst-vertical]
  U6 = SWITCH-SPST-2 [package=switch-spst-vertical]
  U7 = SWITCH-SPST-2 [package=switch-spst-vertical]
  U8 = SWITCH-SPST-2 [package=switch-spst-vertical]
  U9 = SWITCH-SPST-2 [package=switch-spst-vertical]
  PRESSURE4 = OpenSegment Serial Display - 20mm (Blue) [part_number=COM-11647]
  PRESSURE5 = OpenSegment Serial Display - 20mm (Blue) [part_number=COM-11647]
  PRESSURE6 = OpenSegment Serial Display - 20mm (Blue) [part_number=COM-11647]
  PRESSURE7 = OpenSegment Serial Display - 20mm (Blue) [part_number=COM-11647]
  PRESSURE8 = OpenSegment Serial Display - 20mm (Blue) [part_number=COM-11647]
  IC2 = ADS1115 16-bit ADC Breakout
  U10 = POT [package=pot_alpha_rv16af-20]
  U11 = POT [package=pot_alpha_rv16af-20]
  U12 = POT [package=pot_alpha_rv16af-20]
  IC3 = ADS1115 16-bit ADC Breakout
  R10 = Resistor [tolerance=±5% resistance=1k package=THT]
  R11 = Resistor [tolerance=±5% resistance=1k package=THT]
  R12 = Resistor [tolerance=±5% resistance=1k package=THT]

nets:
  GND: MASS1.GND, MASS1.-, IC1.GND, MASS2.GND, MASS2.-, PRESSURE1.GND, PRESSURE1.-, MASS3.GND, MASS3.-, PRESSURE2.GND, PRESSURE2.-, MASS4.GND, MASS4.-, MASS5.-, PRESSURE3.-, MASS6.-, INA1.GND, U7.P, U8.P, U9.P, PRESSURE4.GND, PRESSURE4.-, PRESSURE5.GND, PRESSURE5.-, PRESSURE6.GND, PRESSURE6.-, PRESSURE7.GND, PRESSURE7.-, PRESSURE8.GND, PRESSURE8.-, IC2.GND, U10.E, U11.E, U12.E, IC3.GND
  VCC: MASS1.VCC, MASS1.+, IC1.VIN, IC1.SCL, Part1.HV3, MASS2.VCC, MASS2.+, PRESSURE1.VCC, PRESSURE1.+, MASS3.VCC, MASS3.+, PRESSURE2.+, MASS4.+, MASS5.+, PRESSURE3.VCC, PRESSURE3.SCL#11, PRESSURE3.+, MASS6.+, INA1.VCC, INA1.SCL, INA1.Vin+, PRESSURE4.VCC, PRESSURE4.+, PRESSURE5.VCC, PRESSURE5.+, PRESSURE6.VCC, PRESSURE6.+, PRESSURE7.VCC, PRESSURE7.+, PRESSURE8.VCC, PRESSURE8.+, PRESSURE8.SCL#16, IC2.VDD, IC2.SCL, IC3.VDD, IC3.SCL, R10.Pin_0, R11.Pin_0, R12.Pin_0
  N1: MASS1.SDA, MASS2.SDA#17
  N2: MASS1.SCL, MASS2.SCL#16
  N3: IC1.SDA, Part1.HV4, PRESSURE3.SDA#10, INA1.SDA, PRESSURE8.SDA#17, IC2.SDA, IC3.SDA
  N4: BeagleBone1.VDD_3V3, BeagleBone1.VDD_5V
  N5: BeagleBone1.I2C2_SCL, BeagleBone1.SPIO_D0
  N6: MASS2.SDA#10, PRESSURE1.SDA#17
  N7: MASS2.SCL#11, PRESSURE1.SCL#16
  N8: PRESSURE1.SDA#10, PRESSURE2.SDA#10
  N9: PRESSURE1.SCL#11, PRESSURE2.SCL#11
  N10: MASS3.SDA#10, MASS4.SDA#17
  N11: MASS3.SCL#11, MASS4.SCL#16
  N12: MASS3.SCL#16, MASS5.SCL#16
  N13: MASS3.SDA#17, MASS5.SDA#17
  N14: PRESSURE2.SCL#16, MASS4.SCL#11
  N15: PRESSURE2.SDA#17, MASS4.SDA#10
  N16: MASS5.SDA#10, MASS6.SDA#17
  N17: MASS5.SCL#11, MASS6.SCL#16
  N18: PRESSURE3.SCL#16, MASS6.SCL#11
  N19: PRESSURE3.SDA#17, MASS6.SDA#10
  N20: INA1.Vin-, R1.Pin_0, R2.Pin_0, R3.Pin_0
  N21: R1.Pin_1, U1.O
  N22: R2.Pin_1, U2.O
  N23: R3.Pin_1, U3.O
  N24: R4.Pin_0, R5.Pin_0, R6.Pin_0, U1.P, U2.P, U3.P, IC2.A0
  N25: R4.Pin_1, U4.O
  N26: R5.Pin_1, U5.O
  N27: R6.Pin_1, U6.O
  N28: R7.Pin_0, R8.Pin_0, R9.Pin_0, U4.P, U5.P, U6.P, IC2.A1
  N29: R7.Pin_1, U7.O
  N30: R8.Pin_1, U9.O
  N31: R9.Pin_1, U8.O
  N32: PRESSURE4.SCL, PRESSURE5.SCL#11
  N33: PRESSURE4.SDA, PRESSURE5.SDA#10
  N34: PRESSURE5.SCL#16, PRESSURE6.SCL#11
  N35: PRESSURE5.SDA#17, PRESSURE6.SDA#10
  N36: PRESSURE6.SCL#16, PRESSURE7.SCL#16
  N37: PRESSURE6.SDA#17, PRESSURE7.SDA#17
  N38: PRESSURE7.SDA#10, PRESSURE8.SDA#10
  N39: PRESSURE7.SCL#11, PRESSURE8.SCL#11
  N40: U10.A, R10.Pin_1
  N41: U10.S, IC3.A0
  N42: U11.A, R11.Pin_1
  N43: U11.S, IC3.A1
  N44: U12.A, R12.Pin_1
  N45: U12.S, IC3.A2

notes:
  +5V Rail
  I2C Rail
  0X71
  X-Axis
  Y-Axis
  Z-Axis

custom parts:
  OpenSegment Serial Display - 20mm (Blue): OpenSegment makes it easy to add a large 7-segment display to your project. Because larger 7-segment displays pull more power than a microcontroller is able to drive directly, the OpenSegment has 8 PNP and 4 NPN transistors in order to drive the segments at their maximum brightness! The on-board ATmega328 receives data over multiple digital interfaces (such as TWI, UART and SPI) and does all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
  DIP - 14 pins: A DIP stand-in part for whatever IC you want. With 14 pins on a 300mil dual inline package (DIP) footprint.
  Bi-Directional Logic Level Converter: Description: If you've ever tried to connect a 3.3V device to a 5V system, you know what a challenge it can be. The SparkFun bi-directional logic level converter is a small device that safely steps down 5V signals to 3.3V AND steps up 3.3V to 5V at the same time. This level converter also works with 2.8V and 1.8V devices. What really separates this Logic level converter from our previous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
  BeagleBone Black: BeagleBone Black rev. A5B
  INA219 DC Current Sensor Breakout: INA DC Current Sensor Breakout
  ADS1115 16-bit ADC Breakout: ADS1015 12-bit I2C ADC+PGA Breakout
